# Fritzing sketch 1_24208029386 (saved by Fritzing 1.0.5)
breadboards: 1

parts:
  Part1 = Arduino Uno (Rev3)
  KY-1 = Keyes Relay [package=THT]
  LED1 = smd LED [color="Red (633nm)" package="0603 [SMD]"]

nets:
  N1: Part1.GND, KY-1.power, LED1.cathode
  N2: Part1.D6_PWM, KY-1.ground
  N3: Part1.5V, KY-1.signal, KY-1.C
  N4: KY-1.NC, LED1.anode

custom parts:
  Keyes Relay: The Keyes 5V relay module is suitable for SCM development, home appliance control. It uses a 5V~12V TIL control signal which can control DC / AC signal.
